// Logisim project cdm16.circ as structural Verilog: 1 circuit, main circuit main
module main (
);

  wire cdm_16_1_p1, cdm_16_1_p2, cdm_16_1_p3, cdm_16_1_p4, cdm_16_1_p5, cdm_16_1_p6, cdm_16_1_p7, not_1_out;
  wire [15:0] cdm_16_1_p8, cdm_16_1_p9, controlled_buffer_1_out;

  // Probe on cdm_16_1_p2
  // Probe on cdm_16_1_p1
  // CdM_16 cdm_16_1: pin names not known; wires that end beside it: cdm_16_1_p1, cdm_16_1_p2, cdm_16_1_p3, cdm_16_1_p4, cdm_16_1_p5, cdm_16_1_p6, cdm_16_1_p7, cdm_16_1_p8, cdm_16_1_p9
  Clock clock_1 (.out(cdm_16_1_p3));
  // Probe on cdm_16_1_p4
  assign controlled_buffer_1_out = not_1_out ? cdm_16_1_p8 : 16'bz;  // Controlled_Buffer controlled_buffer_1
  not not_1 (not_1_out, cdm_16_1_p6);
  assign cdm_16_1_p9 = cdm_16_1_p6 ? controlled_buffer_1_out : 16'bz;  // Controlled_Buffer controlled_buffer_2
  // Probe on cdm_16_1_p7
  Pull_Resistor pull_resistor_1 ();  // open: node
  // RAM ram_1: pin names not known; wires that end beside it: cdm_16_1_p7, 1'b1, cdm_16_1_p5, cdm_16_1_p3, cdm_16_1_p6, controlled_buffer_1_out
  // Probe on controlled_buffer_1_out
endmodule
