// Logisim project cdm_debug.circ as structural Verilog: 2 circuits, main circuit main
module main (
);

  wire cdm_16_1_p1, cdm_16_1_p2, cdm_16_1_p3, cdm_16_1_p4, cdm_16_1_p5, cdm_16_1_p6, cdm_16_1_p7, not_1_out;
  wire [15:0] cdm_16_1_p8, cdm_16_1_p9, controlled_buffer_1_out;

  // Probe on cdm_16_1_p2
  // Probe on cdm_16_1_p1
  // CdM_16 cdm_16_1: pin names not known; wires that end beside it: cdm_16_1_p1, cdm_16_1_p2, cdm_16_1_p3, cdm_16_1_p4, cdm_16_1_p5, cdm_16_1_p6, cdm_16_1_p7, cdm_16_1_p8, cdm_16_1_p9
  Clock clock_1 (.out(cdm_16_1_p3));
  // Probe on cdm_16_1_p4
  assign controlled_buffer_1_out = not_1_out ? cdm_16_1_p8 : 16'bz;  // Controlled_Buffer controlled_buffer_1
  not not_1 (not_1_out, cdm_16_1_p6);
  assign cdm_16_1_p9 = cdm_16_1_p6 ? controlled_buffer_1_out : 16'bz;  // Controlled_Buffer controlled_buffer_2
  // Probe on cdm_16_1_p7
  Pull_Resistor pull_resistor_1 ();  // open: node
  // RAM ram_1: pin names not known; wires that end beside it: cdm_16_1_p7, 1'b1, cdm_16_1_p5, cdm_16_1_p3, cdm_16_1_p6, controlled_buffer_1_out
  // Probe on controlled_buffer_1_out
endmodule

module gamepad_fix_misses (
  input  checker_select,
  input  clock,
  input  left_up,
  input  [15:0] adress_bus,
  input  right_up,
  input  right_down,
  input  left_down,
  input  finnish_turn,
  output is_active,
  output [15:0] data,
  output [5:0] raw_state,
  output [5:0] register_state
);

  wire and_1_out, d_ff_1_q, d_ff_2_q, d_ff_3_q, d_ff_4_q, d_ff_5_q, d_ff_6_q, d_ff_7_q, d_ff_8_q, d_ff_9_q,
       d_ff_10_q, d_ff_11_q, d_ff_12_q, not_1_out, or_7_out, register_1_q, register_2_q, register_3_q,
       register_5_q, register_6_q, register_7_q, register_8_q, register_9_q, register_10_q, reset1, reset2;
  wire [5:0] register_13_q, register_14_q;
  wire [15:15] pull_resistor_1_node;

  Register #(.width(1)) register_1 (.D(is_active), .Q(register_1_q), .clk(clock));  // open: en, clr
  D_Flip_Flop d_ff_1 (.clk(left_up), .D(1'b1), .Q(d_ff_1_q), .reset(reset1));  // open: Qn, preset, en
  D_Flip_Flop d_ff_2 (.clk(left_up), .D(1'b1), .Q(d_ff_2_q), .reset(reset2));  // open: Qn, preset, en
  D_Flip_Flop d_ff_3 (.clk(left_down), .D(1'b1), .Q(d_ff_3_q), .reset(reset1));  // open: Qn, preset, en
  D_Flip_Flop d_ff_4 (.clk(left_down), .D(1'b1), .Q(d_ff_4_q), .reset(reset2));  // open: Qn, preset, en
  Register #(.width(1)) register_2 (.D(register_1_q), .Q(register_2_q), .clk(clock));  // open: en, clr
  or or_1 (raw_state[2], d_ff_1_q, d_ff_2_q);
  or or_2 (raw_state[4], d_ff_3_q, d_ff_4_q);
  Register #(.width(1)) register_3 (.D(register_2_q), .Q(register_3_q), .clk(clock));  // open: en, clr
  Register #(.width(1)) register_4 (.D(register_3_q), .Q(reset1), .clk(clock));  // open: en, clr
  D_Flip_Flop d_ff_5 (.clk(right_up), .D(1'b1), .Q(d_ff_5_q), .reset(reset1));  // open: Qn, preset, en
  D_Flip_Flop d_ff_6 (.clk(right_up), .D(1'b1), .Q(d_ff_6_q), .reset(reset2));  // open: Qn, preset, en
  D_Flip_Flop d_ff_7 (.clk(right_down), .D(1'b1), .Q(d_ff_7_q), .reset(reset1));  // open: Qn, preset, en
  D_Flip_Flop d_ff_8 (.clk(right_down), .D(1'b1), .Q(d_ff_8_q), .reset(reset2));  // open: Qn, preset, en
  Register #(.width(1)) register_5 (.D(reset1), .Q(register_5_q), .clk(clock));  // open: en, clr
  Register #(.width(1)) register_6 (.D(register_5_q), .Q(register_6_q), .clk(clock));  // open: en, clr
  or or_3 (raw_state[1], d_ff_5_q, d_ff_6_q);
  or or_4 (raw_state[3], d_ff_7_q, d_ff_8_q);
  Register #(.width(1)) register_7 (.D(register_6_q), .Q(register_7_q), .clk(clock));  // open: en, clr
  D_Flip_Flop d_ff_9 (.clk(checker_select), .D(1'b1), .Q(d_ff_9_q), .reset(reset1));  // open: Qn, preset, en
  D_Flip_Flop d_ff_10 (.clk(checker_select), .D(1'b1), .Q(d_ff_10_q), .reset(reset2));  // open: Qn, preset, en
  D_Flip_Flop d_ff_11 (.clk(finnish_turn), .D(1'b1), .Q(d_ff_11_q), .reset(reset1));  // open: Qn, preset, en
  D_Flip_Flop d_ff_12 (.clk(finnish_turn), .D(1'b1), .Q(d_ff_12_q), .reset(reset2));  // open: Qn, preset, en
  Register #(.width(1)) register_8 (.D(register_7_q), .Q(register_8_q), .clk(clock));  // open: en, clr
  or or_5 (raw_state[0], d_ff_9_q, d_ff_10_q);
  or or_6 (raw_state[5], d_ff_11_q, d_ff_12_q);
  Register #(.width(1)) register_9 (.D(register_8_q), .Q(register_9_q), .clk(clock));  // open: en, clr
  Register #(.width(1)) register_10 (.D(register_9_q), .Q(register_10_q), .clk(clock));  // open: en, clr
  // Probe on register_state
  Register #(.width(6)) register_11 (.D(raw_state), .en(1'b1), .Q(register_state), .clk(clock));  // open: clr
  Register #(.width(1)) register_12 (.D(register_10_q), .Q(reset2), .clk(clock));  // open: en, clr
  not not_1 (not_1_out, adress_bus[0]);
  and and_1 (and_1_out, not_1_out, adress_bus[1], adress_bus[2], adress_bus[3], adress_bus[4], adress_bus[5], adress_bus[6], adress_bus[7], adress_bus[9], adress_bus[10], adress_bus[11], adress_bus[12], adress_bus[13], adress_bus[14], adress_bus[15], adress_bus[8]);
  or or_7 (or_7_out, register_state[5], register_state[4], register_state[3], register_state[1], register_state[0], register_state[2]);
  and and_2 (is_active, and_1_out, or_7_out);
  Register #(.width(6)) register_13 (.Q(register_13_q), .clk(clock));  // open: D, en, clr
  Pull_Resistor pull_resistor_1 (.node(pull_resistor_1_node[15]));
  Register #(.width(6)) register_14 (.D(register_13_q), .Q(register_14_q), .clk(clock));  // open: en, clr
  Register #(.width(6)) register_15 (.D(register_14_q), .clk(clock));  // open: en, Q, clr
  assign data = is_active ? {{10{pull_resistor_1_node[15]}}, register_state} : 16'bz;  // Controlled_Buffer controlled_buffer_1

  // Other names for the same wires on the sheet: data_bus[15:0] = data; finish_turn = finnish_turn
endmodule
