// Logisim project control_device_backup.circ as structural Verilog: 4 circuits, main circuit main
module main (
);

  wire and_1_out, and_2_out, cdm_16_1_p1, cdm_16_1_p2, cdm_16_1_p4, cdm_16_1_p5, cdm_16_1_p6, cdm_16_1_p7,
       checker_select_1_led1, checker_select_1_led2, checker_select_1_led3, checker_select_1_led4,
       checker_select_1_led5, checker_select_1_led6, checker_select_1_led7, checker_select_1_led8,
       checker_select_1_leda, checker_select_1_ledb, checker_select_1_ledc, checker_select_1_ledd,
       checker_select_1_lede, checker_select_1_ledf, checker_select_1_ledg, checker_select_1_ledh, clock,
       is_active, memory_select, nor_1_out, not_1_out, read, \двигать_шашку_out , \лево_верх_out ,
       \лево_низ_out , \право_верх_out , \право_низ_out , \прекратить_ход_out ;
  wire [7:0] game_status_1_leds;
  wire [15:0] adress_bus, data_bus, data_in, data_out, ram_1_p6, transistor_1_out;

  // Probe on cdm_16_1_p7
  // Probe on cdm_16_1_p6
  // Probe on cdm_16_1_p5
  // Probe on cdm_16_1_p4
  // Probe on cdm_16_1_p2
  // Probe on cdm_16_1_p1
  // CdM_16 cdm_16_1: pin names not known; wires that end beside it: cdm_16_1_p1, cdm_16_1_p2, clock, cdm_16_1_p4, cdm_16_1_p5, cdm_16_1_p6, cdm_16_1_p7, memory_select, read, adress_bus, data_out, data_in
  Clock clock_1 (.out(clock));
  checker_select checker_select_1 (
    .clock(clock), .data(data_bus), .adress(adress_bus), .led1(checker_select_1_led1),
    .leda(checker_select_1_leda), .led2(checker_select_1_led2), .ledb(checker_select_1_ledb),
    .led3(checker_select_1_led3), .ledc(checker_select_1_ledc), .led4(checker_select_1_led4),
    .ledd(checker_select_1_ledd), .led5(checker_select_1_led5), .lede(checker_select_1_lede),
    .led6(checker_select_1_led6), .ledf(checker_select_1_ledf), .led7(checker_select_1_led7),
    .ledg(checker_select_1_ledg), .led8(checker_select_1_led8), .ledh(checker_select_1_ledh),
    .read_write_prime(read));
  not nor_1 (nor_1_out, is_active);  // NOR_Gate
  LED led_1 (.in(checker_select_1_ledh));
  LED led_2 (.in(checker_select_1_ledg));
  LED led_3 (.in(checker_select_1_ledf));
  LED led_4 (.in(checker_select_1_ledd));
  LED led_5 (.in(checker_select_1_lede));
  LED led_6 (.in(checker_select_1_ledc));
  LED led_7 (.in(checker_select_1_leda));
  LED led_8 (.in(checker_select_1_ledb));
  assign data_bus = not_1_out ? transistor_1_out : 16'bz;  // Controlled_Buffer controlled_buffer_1
  Transistor #(.\type ("n"), .width(16)) transistor_1 (.in(data_out), .out(transistor_1_out), .gate(nor_1_out));
  not not_1 (not_1_out, read);
  assign data_in = read ? data_bus : 16'bz;  // Controlled_Buffer controlled_buffer_2
  LED led_9 (.in(checker_select_1_led1));
  LED led_10 (.in(checker_select_1_led2));
  LED led_11 (.in(checker_select_1_led3));
  LED led_12 (.in(checker_select_1_led4));
  LED led_13 (.in(checker_select_1_led5));
  LED led_14 (.in(checker_select_1_led6));
  LED led_15 (.in(checker_select_1_led7));
  LED led_16 (.in(checker_select_1_led8));
  // RAM ram_1: pin names not known; wires that end beside it: adress_bus, 1'b1, memory_select, clock, read, ram_1_p6
  and and_1 (and_1_out, read, ~is_active);  // AND_Gate
  assign data_bus = and_1_out ? ram_1_p6 : 16'bz;  // Controlled_Buffer controlled_buffer_3
  assign ram_1_p6 = and_2_out ? data_bus : 16'bz;  // Controlled_Buffer controlled_buffer_4
  and and_2 (and_2_out, ~read, ~is_active);  // AND_Gate
  game_status game_status_1 (
    .clock(clock), .adress(adress_bus), .read(read), .data(data_bus), .leds(game_status_1_leds));
  gamepad gamepad_1 (
    .checker_select(\двигать_шашку_out ), .clock(clock), .is_active(is_active), .left_up(\лево_верх_out ),
    .adress_bus(adress_bus), .data(data_bus), .right_up(\право_верх_out ), .right_down(\право_низ_out ),
    .left_down(\лево_низ_out ), .finnish_turn(\прекратить_ход_out ));
  Button \u_двигать_шашку  (.out(\двигать_шашку_out ));
  Button \u_прекратить_ход  (.out(\прекратить_ход_out ));
  LED _1__INVALID_DIRECTION (.in(game_status_1_leds[1]));
  LED _2__YOUR_TURN__CHOOSE_CHECKER (.in(game_status_1_leds[2]));
  LED _3__YOUR_TURN__CHOOSE_CHECKER (.in(game_status_1_leds[3]));
  LED _4__OPPONENT_S_TURN (.in(game_status_1_leds[4]));
  LED _5__YOU_WON (.in(game_status_1_leds[5]));
  LED _6__YOU_LOST (.in(game_status_1_leds[6]));
  LED _8__DRAW (.in(game_status_1_leds[7]));
  Button \u_лево_верх  (.out(\лево_верх_out ));
  Button \u_лево_низ  (.out(\лево_низ_out ));
  Button \u_право_верх  (.out(\право_верх_out ));
  Button \u_право_низ  (.out(\право_низ_out ));

  // Notes on the sheet:
  //   блокировка процессора
  //   блокировка памяти
endmodule

module gamepad (
  input  checker_select,
  input  clock,
  input  left_up,
  input  [15:0] adress_bus,
  input  right_up,
  input  right_down,
  input  left_down,
  input  finnish_turn,
  output is_active,
  output [15:0] data
);

  wire not_1_out, pull_resistor_1_node, register_1_q, register_2_q, reset_state;
  wire [5:0] d_ff_3_q, register_3_q;
  wire [15:15] pull_resistor_2_node;

  Register #(.width(1)) register_1 (
    .D(is_active), .en(1'b1), .Q(register_1_q), .clk(clock), .clr(pull_resistor_1_node));
  Register #(.width(1), .trigger("low")) register_2 (
    .D(register_1_q), .en(1'b1), .Q(register_2_q), .clk(clock), .clr(pull_resistor_1_node));
  Pull_Resistor pull_resistor_1 (.node(pull_resistor_1_node));
  and and_1 (reset_state, 1'b1, register_2_q);
  D_Flip_Flop d_ff_1 (.clk(left_up), .D(1'b1), .Q(d_ff_3_q[2]), .reset(reset_state));  // open: Qn, preset, en
  D_Flip_Flop d_ff_2 (.clk(left_down), .D(1'b1), .Q(d_ff_3_q[4]), .reset(reset_state));  // open: Qn, preset, en
  D_Flip_Flop d_ff_3 (.clk(checker_select), .D(1'b1), .Q(d_ff_3_q[0]), .reset(reset_state));  // open: Qn, preset, en
  D_Flip_Flop d_ff_4 (.clk(finnish_turn), .D(1'b1), .Q(d_ff_3_q[5]), .reset(reset_state));  // open: Qn, preset, en
  D_Flip_Flop d_ff_5 (.clk(right_up), .D(1'b1), .Q(d_ff_3_q[1]), .reset(reset_state));  // open: Qn, preset, en
  D_Flip_Flop d_ff_6 (.clk(right_down), .D(1'b1), .Q(d_ff_3_q[3]), .reset(reset_state));  // open: Qn, preset, en
  // Probe on register_3_q
  Register #(.width(6)) register_3 (
    .D(d_ff_3_q), .en(1'b1), .Q(register_3_q), .clk(clock), .clr(pull_resistor_2_node[15]));
  Pull_Resistor pull_resistor_2 (.node(pull_resistor_2_node[15]));
  not not_1 (not_1_out, adress_bus[0]);
  and and_2 (is_active, not_1_out, adress_bus[1], adress_bus[2], adress_bus[3], adress_bus[4], adress_bus[5], adress_bus[6], adress_bus[7], adress_bus[9], adress_bus[10], adress_bus[11], adress_bus[12], adress_bus[13], adress_bus[14], adress_bus[15], adress_bus[8]);
  assign data = is_active ? {{10{pull_resistor_2_node[15]}}, register_3_q} : 16'bz;  // Controlled_Buffer controlled_buffer_1

  // Other names for the same wires on the sheet: data_bus[15:0] = data

  // Notes on the sheet:
  //   inputs
  //   outputs
  //   buttons
endmodule

module checker_select (
  input  clock,
  input  [15:0] data,
  input  [15:0] adress,
  input  read_write_prime,
  output led1,
  output leda,
  output led2,
  output ledb,
  output led3,
  output ledc,
  output led4,
  output ledd,
  output led5,
  output lede,
  output led6,
  output ledf,
  output led7,
  output ledg,
  output led8,
  output ledh
);

  wire enable;
  wire [2:0] register_1_q, register_2_q;

  and and_1 (enable, ~adress[0], ~adress[1], adress[2], adress[3], adress[4], adress[5], adress[6], adress[7], adress[8], adress[9], adress[10], adress[11], adress[12], adress[13], adress[14], adress[15], ~read_write_prime);  // AND_Gate
  Register #(.width(3)) register_1 (.D(data[5:3]), .en(enable), .Q(register_1_q), .clk(clock), .clr(1'b0));
  Decoder #(.select(3)) decoder_1 (
    .out0(leda), .out1(ledb), .out2(ledc), .out3(ledd), .out4(lede), .out5(ledf), .out6(ledg), .out7(ledh),
    .sel(register_1_q));  // open: en
  Decoder #(.select(3)) decoder_2 (
    .out0(led1), .out1(led2), .out2(led3), .out3(led4), .out4(led5), .out5(led6), .out6(led7), .out7(led8),
    .sel(register_2_q));  // open: en
  Register #(.width(3)) register_2 (.D(data[2:0]), .en(enable), .Q(register_2_q), .clk(clock), .clr(1'b0));
endmodule

module game_status (
  input  clock,
  input  [15:0] adress,
  input  read,
  input  [15:0] data,
  output [7:0] leds
);

  wire is_active;
  wire [7:0] decoder_1_out0;

  and and_1 (is_active, ~adress[0], adress[1], ~adress[2], adress[3], adress[4], adress[5], adress[6], adress[7], adress[8], adress[9], adress[10], adress[11], adress[12], adress[13], adress[14], adress[15], ~read);  // AND_Gate
  Decoder #(.select(3)) decoder_1 (
    .out0(decoder_1_out0[0]), .out1(decoder_1_out0[1]), .out2(decoder_1_out0[2]), .out3(decoder_1_out0[3]),
    .out4(decoder_1_out0[4]), .out5(decoder_1_out0[5]), .out6(decoder_1_out0[6]), .out7(decoder_1_out0[7]),
    .sel(data[2:0]), .en(is_active));
  Register register_1 (.D(decoder_1_out0), .en(is_active), .Q(leds), .clk(clock));  // open: clr
  // Probe on leds
endmodule
