// Logisim project project-checkers.circ as structural Verilog: 8 circuits, main circuit main
module main (
);

  wire button_1_out, clock, comparator_1_lt, comparator_2_eq, comparator_3_eq, deshifrator, dev_read,
       dev_write, mem, not_1_out, read;
  wire [5:0] undriven;
  wire [15:0] address_bus, bit_extender_1_out, data_bus, register_1_q;

  // Debugger debugger_1: pin names not known
  not not_1 (not_1_out, read);
  Comparator #(.width(16), .mode("unsigned")) comparator_1 (
    .a(address_bus), .b(16'h8000), .lt(comparator_1_lt));  // open: gt, eq
  Comparator #(.width(16), .mode("unsigned")) comparator_2 (
    .a(address_bus), .b(16'h8000), .eq(comparator_2_eq));  // open: gt, lt
  and and_1 (deshifrator, mem, comparator_1_lt);
  and and_2 (dev_write, mem, comparator_2_eq, not_1_out);
  Comparator #(.width(16), .mode("unsigned")) comparator_3 (
    .a(address_bus), .b(16'h8002), .eq(comparator_3_eq));  // open: gt, lt
  assign bit_extender_1_out = {{15{1'b0}}, button_1_out};  // Bit_Extender bit_extender_1
  Button button_1 (.out(button_1_out));
  and and_3 (dev_read, mem, comparator_3_eq, read);
  assign data_bus = dev_read ? bit_extender_1_out : 16'bz;  // Controlled_Buffer controlled_buffer_1
  Register #(.width(16)) register_1 (.D(data_bus), .en(dev_write), .Q(register_1_q), .clk(clock));  // open: clr
  DotMatrix #(.matrixcols(1), .matrixrows(16)) dotmatrix_1 (.col0(register_1_q));
  DotMatrix #(.matrixcols(27), .matrixrows(18)) dotmatrix_2 (
    .col0({12'h3f, undriven}), .col1({12'h3f, undriven}), .col2({12'h3f, undriven}),
    .col3({12'h3f, undriven}), .col4({12'h3f, undriven}), .col5({12'h3f, undriven}),
    .col6({12'h3f, undriven}), .col7({12'h3f, undriven}), .col8({12'h3f, undriven}),
    .col9({12'h3f, undriven}), .col10({12'h3f, undriven}), .col11({12'h3f, undriven}),
    .col12({12'h3f, undriven}), .col13({12'h3f, undriven}), .col14({12'h3f, undriven}),
    .col15({12'h3f, undriven}), .col16({12'h3f, undriven}), .col17({12'h3f, undriven}),
    .col18({12'h3f, undriven}), .col19({12'h3f, undriven}), .col20({12'h3f, undriven}),
    .col21({12'h3f, undriven}), .col22({12'h3f, undriven}), .col23({12'h3f, undriven}),
    .col24({12'h3f, undriven}), .col25({12'h3f, undriven}), .col26({12'h3f, undriven}));
endmodule

module square (
  input  [3:0] number0_4,
  output [3:0] bus_0,
  output [3:0] bus_1,
  output [3:0] bus_2,
  output [3:0] bus_3
);

  wire [1:1] type_2;
  wire [2:0] bit_extender_1_out;
  wire [2:1] type_1;

  Bit_Extender #(.in_width(4), .out_width(3)) bit_extender_1 (.in(number0_4), .out(bit_extender_1_out));
  Multiplexer #(.select(3), .width(4)) multiplexer_1 (
    .in0(4'b0000), .in1(4'b0110), .in2({1'b0, type_1, 1'b0}), .in3(4'b0110), .in4({1'b0, type_1, 1'b0}),
    .in5(4'b1111), .in6(4'b1111), .in7(4'b1111), .out(bus_1), .sel(bit_extender_1_out));  // open: en
  // Probe on bus_1
  Multiplexer #(.select(3), .width(4)) multiplexer_2 (
    .in0(4'b0000), .in1(4'b0110), .in2({1'b0, type_1, 1'b0}), .in3(4'b0010), .in4({2'b00, type_2[1], 1'b0}),
    .in5(4'b1111), .in6(4'b1111), .in7(4'b1111), .out(bus_2), .sel(bit_extender_1_out));  // open: en
  Multiplexer #(.select(3), .width(4)) multiplexer_3 (
    .in0(4'b0000), .in1(4'b0000), .in2(4'b0000), .in3(4'b0000), .in4(4'b0000), .in5(4'b1111), .in6(4'b1111),
    .in7(4'b1111), .out(bus_0), .sel(bit_extender_1_out));  // open: en

  assign bus_3 = bus_0;

  // Notes on the sheet:
  //   0 - пустая клетка
  //   1 - белая шашка
  //   2 - черная шашка
  //   3 - белая дамка
  //   4 - черная дамка
endmodule

module square_32 (
  input  [31:0] bus_0,
  output [31:0] bus_0_2,
  output [31:0] bus_0_3,
  output [31:0] bus_0_4,
  output [31:0] bus_0_5
);

  square square_1 (
    .number0_4(bus_0[3:0]), .bus_0(bus_0_2[3:0]), .bus_1(bus_0_3[3:0]), .bus_2(bus_0_4[3:0]),
    .bus_3(bus_0_5[3:0]));
  square square_2 (
    .number0_4(bus_0[7:4]), .bus_0(bus_0_2[7:4]), .bus_1(bus_0_3[7:4]), .bus_2(bus_0_4[7:4]),
    .bus_3(bus_0_5[7:4]));
  square square_3 (
    .number0_4(bus_0[11:8]), .bus_0(bus_0_2[11:8]), .bus_1(bus_0_3[11:8]), .bus_2(bus_0_4[11:8]),
    .bus_3(bus_0_5[11:8]));
  square square_4 (
    .number0_4(bus_0[15:12]), .bus_0(bus_0_2[15:12]), .bus_1(bus_0_3[15:12]), .bus_2(bus_0_4[15:12]),
    .bus_3(bus_0_5[15:12]));
  square square_5 (
    .number0_4(bus_0[19:16]), .bus_0(bus_0_2[19:16]), .bus_1(bus_0_3[19:16]), .bus_2(bus_0_4[19:16]),
    .bus_3(bus_0_5[19:16]));
  square square_6 (
    .number0_4(bus_0[23:20]), .bus_0(bus_0_2[23:20]), .bus_1(bus_0_3[23:20]), .bus_2(bus_0_4[23:20]),
    .bus_3(bus_0_5[23:20]));
  square square_7 (
    .number0_4(bus_0[27:24]), .bus_0(bus_0_2[27:24]), .bus_1(bus_0_3[27:24]), .bus_2(bus_0_4[27:24]),
    .bus_3(bus_0_5[27:24]));
  square square_8 (
    .number0_4(bus_0[31:28]), .bus_0(bus_0_2[31:28]), .bus_1(bus_0_3[31:28]), .bus_2(bus_0_4[31:28]),
    .bus_3(bus_0_5[31:28]));
endmodule

module control_device (
  input  \Обнулитель 
);

  wire and_1_out, clock_1_out, pull_resistor_1_node, \двигать_шашку_out , \лево_верх_out , \лево_низ_out ,
       \право_верх_out , \право_низ_out , \прекратить_ход_out ;
  wire [5:0] d_ff_3_q, register_1_q;

  Button \u_лево_верх  (.out(\лево_верх_out ));
  D_Flip_Flop d_ff_1 (.clk(\лево_верх_out ), .D(1'b1), .Q(d_ff_3_q[2]), .reset(and_1_out));  // open: Qn, preset, en
  D_Flip_Flop d_ff_2 (.clk(\лево_низ_out ), .D(1'b1), .Q(d_ff_3_q[4]), .reset(and_1_out));  // open: Qn, preset, en
  Button \u_лево_низ  (.out(\лево_низ_out ));
  and and_1 (and_1_out, 1'b1, \Обнулитель );
  Button \u_двигать_шашку  (.out(\двигать_шашку_out ));
  Button \u_прекратить_ход  (.out(\прекратить_ход_out ));
  D_Flip_Flop d_ff_3 (.clk(\двигать_шашку_out ), .D(1'b1), .Q(d_ff_3_q[0]), .reset(and_1_out));  // open: Qn, preset, en
  Button \u_право_низ  (.out(\право_низ_out ));
  D_Flip_Flop d_ff_4 (
    .clk(\прекратить_ход_out ), .D(1'b1), .Q(d_ff_3_q[5]), .reset(and_1_out));  // open: Qn, preset, en
  Button \u_право_верх  (.out(\право_верх_out ));
  D_Flip_Flop d_ff_5 (.clk(\право_верх_out ), .D(1'b1), .Q(d_ff_3_q[1]), .reset(and_1_out));  // open: Qn, preset, en
  D_Flip_Flop d_ff_6 (.clk(\право_низ_out ), .D(1'b1), .Q(d_ff_3_q[3]), .reset(and_1_out));  // open: Qn, preset, en
  Clock clock_1 (.out(clock_1_out));
  // Probe on register_1_q
  Register #(.width(6)) register_1 (
    .D(d_ff_3_q), .en(1'b1), .Q(register_1_q), .clk(clock_1_out), .clr(pull_resistor_1_node));
  Pull_Resistor pull_resistor_1 (.node(pull_resistor_1_node));
endmodule

module state (
  input  [2:0] \input ,
  input  [2:0] \тек_сост 
);

  wire decoder_1_out1, decoder_1_out2, decoder_1_out3, decoder_1_out4, decoder_1_out5, decoder_1_out6,
       decoder_2_out0, decoder_2_out1, decoder_2_out2, decoder_2_out3, decoder_2_out4, decoder_2_out5,
       decoder_2_out6;

  Decoder #(.select(3)) decoder_1 (
    .out1(decoder_1_out1), .out2(decoder_1_out2), .out3(decoder_1_out3), .out4(decoder_1_out4),
    .out5(decoder_1_out5), .out6(decoder_1_out6), .sel(\input ));  // open: out0, out7, en
  LED led_1 (.in(decoder_1_out1));
  LED led_2 (.in(decoder_1_out2));
  LED led_3 (.in(decoder_1_out3));
  LED led_4 (.in(decoder_1_out4));
  LED led_5 (.in(decoder_1_out5));
  LED led_6 (.in(decoder_1_out6));
  Decoder #(.select(3)) decoder_2 (
    .out0(decoder_2_out0), .out1(decoder_2_out1), .out2(decoder_2_out2), .out3(decoder_2_out3),
    .out4(decoder_2_out4), .out5(decoder_2_out5), .out6(decoder_2_out6), .sel(\тек_сост ));  // open: out7, en
  LED led_7 (.in(decoder_2_out0));
  LED led_8 (.in(decoder_2_out1));
  LED led_9 (.in(decoder_2_out2));
  LED led_10 (.in(decoder_2_out3));
  LED led_11 (.in(decoder_2_out4));
  LED led_12 (.in(decoder_2_out5));
  LED led_13 (.in(decoder_2_out6));

  // Notes on the sheet:
  //   1. IMPOSSIBLE MOVE
  //   2. YOUR TURN
  //   3. OPPONENT TURN
  //   4. YOU WIN
  //   5. YOU LOSE
  //   6. DRAW
  //   0. IMPOSSIBLE MOVE
  //   3. OPPONENT TURN
  //   4. YOU WIN
  //   5. YOU LOSE
  //   6. DRAW
  //   1. YOUR TURN, CHOOSE CHECKER
  //   2. YOUR TURN, CHOOSE DIRECTION
endmodule

module timer__no_must (
);

  wire clock_1_out;
  wire [3:0] bit_extender_1_out, bit_extender_2_out, bit_extender_3_out;
  wire [15:0] adder_1_out, counter_1_q, divider_1_out, divider_1_rem, divider_2_out, divider_2_rem,
       divider_3_out, divider_3_rem, multiplier_1_out;

  // Probe on 16'h12c
  Multiplier #(.width(16)) multiplier_1 (.a(16'h12c), .b(16'h10), .out(multiplier_1_out));  // open: cin, cout
  Adder #(.width(16)) adder_1 (.a(multiplier_1_out), .b(counter_1_q), .out(adder_1_out));  // open: cin, cout
  Counter #(.width(16), .max('hffff)) counter_1 (
    .load(1'b1), .Q(counter_1_q), .clk(clock_1_out));  // open: D, count, carry, clr
  Clock clock_1 (.out(clock_1_out));
  // Probe on 16'h10
  Hex_Digit_Display hex_digit_display_1 (.value(bit_extender_1_out), .dp(1'b1));
  Bit_Extender #(.in_width(16), .out_width(4)) bit_extender_1 (.in(divider_2_out), .out(bit_extender_1_out));
  Divider #(.width(16)) divider_1 (
    .a(adder_1_out), .b(16'h10), .out(divider_1_out), .rem(divider_1_rem));  // open: upper
  Hex_Digit_Display hex_digit_display_2 (.value(bit_extender_2_out));  // open: dp
  Hex_Digit_Display hex_digit_display_3 (.value(bit_extender_3_out));  // open: dp
  Divider #(.width(16)) divider_2 (
    .a(divider_1_out), .b(16'h3c), .out(divider_2_out), .rem(divider_2_rem));  // open: upper
  Bit_Extender #(.in_width(16), .out_width(4)) bit_extender_2 (.in(divider_3_out), .out(bit_extender_2_out));
  Bit_Extender #(.in_width(16), .out_width(4)) bit_extender_3 (.in(divider_3_rem), .out(bit_extender_3_out));
  Divider #(.width(16)) divider_3 (
    .a(divider_2_rem), .b(16'ha), .out(divider_3_out), .rem(divider_3_rem));  // open: upper

  // Notes on the sheet:
  //   это таймер в секундах, чтобы правильно работал надо константу снизу (где число 16), всегда делать равной половине частоты
endmodule

module board (
);

  wire act_0, act_1, act_2, act_3, act_4, act_5, act_6, act_7, clock, comparator_2_eq, comparator_3_lt,
       comparator_4_eq, comparator_5_eq, comparator_6_eq, comparator_7_eq, comparator_8_eq, comparator_9_eq,
       comparator_10_eq, comparator_11_eq, deshifrator, dev_wr2, DEV_write, is_board, is_ready, mem,
       not_1_out, not_2_out, read, word;
  wire [3:0] bit_extender_1_out, register_1_q, register_2_q, register_3_q, register_4_q, register_5_q,
       register_6_q, register_7_q, register_8_q;
  wire [15:0] address_bus, cdm16_1_p6, cdm16_1_p7, data_bus, ram_2_data;
  wire [31:0] square_32_1_bus_0_2, square_32_1_bus_0_3, square_32_1_bus_0_4, square_32_1_bus_0_5,
       square_32_2_bus_0_2, square_32_2_bus_0_3, square_32_2_bus_0_4, square_32_2_bus_0_5,
       square_32_3_bus_0_2, square_32_3_bus_0_3, square_32_3_bus_0_4, square_32_3_bus_0_5,
       square_32_4_bus_0_2, square_32_4_bus_0_3, square_32_4_bus_0_4, square_32_4_bus_0_5,
       square_32_5_bus_0_2, square_32_5_bus_0_3, square_32_5_bus_0_4, square_32_5_bus_0_5,
       square_32_6_bus_0_2, square_32_6_bus_0_3, square_32_6_bus_0_4, square_32_6_bus_0_5,
       square_32_7_bus_0_2, square_32_7_bus_0_3, square_32_7_bus_0_4, square_32_7_bus_0_5,
       square_32_8_bus_0_2, square_32_8_bus_0_3, square_32_8_bus_0_4, square_32_8_bus_0_5,
       square_32_9_bus_0_2, square_32_9_bus_0_3, square_32_9_bus_0_4, square_32_9_bus_0_5, \ооо_1_bus_0 ;

  Clock clock_1 (.out(clock));
  // cdm16 cdm16_1: pin names not known; wires that end beside it: clock, mem, read, word, address_bus, cdm16_1_p6, cdm16_1_p7
  Comparator #(.width(9), .mode("unsigned")) comparator_1 (
    .a(address_bus[15:7]), .b(9'h1e0), .eq(is_board));  // open: gt, lt
  and and_1 (is_ready, is_board, read);
  // Probe on address_bus
  assign data_bus = not_1_out ? cdm16_1_p6 : 16'bz;  // Controlled_Buffer controlled_buffer_1
  not not_1 (not_1_out, read);
  assign cdm16_1_p7 = read ? data_bus : 16'bz;  // Controlled_Buffer controlled_buffer_2
  and and_2 (dev_wr2, DEV_write, clock);
  // Probe on data_bus
  // RAM ram_1: pin names not known; wires that end beside it: address_bus, word, deshifrator, clock, read, data_bus
  Comparator #(.width(16), .mode("unsigned")) comparator_2 (
    .a(address_bus), .b(16'hf000), .eq(comparator_2_eq));  // open: gt, lt
  not not_2 (not_2_out, read);
  // Probe on address_bus[6:1]
  and and_3 (DEV_write, comparator_2_eq, mem, not_2_out);
  RAM #(.addrWidth(6), .dataWidth(16)) ram_2 (
    .addr(address_bus[6:1]), .data(ram_2_data), .sel(is_board), .clk(clock), .ld(DEV_write));  // open: clr
  Comparator #(.width(16), .mode("unsigned")) comparator_3 (
    .a(address_bus), .b(16'h8000), .lt(comparator_3_lt));  // open: gt, eq
  // Probe on ram_2_data
  assign ram_2_data = read ? data_bus : 16'bz;  // Controlled_Buffer controlled_buffer_3
  Bit_Extender #(.in_width(16), .out_width(4)) bit_extender_1 (.in(ram_2_data), .out(bit_extender_1_out));
  and and_4 (deshifrator, mem, comparator_3_lt);
  DotMatrix #(.matrixcols(4), .matrixrows(32)) dotmatrix_1 (
    .col0(square_32_2_bus_0_2), .col1(square_32_2_bus_0_3), .col2(square_32_2_bus_0_4),
    .col3(square_32_2_bus_0_5));
  DotMatrix #(.matrixcols(4), .matrixrows(32)) dotmatrix_2 (
    .col0(square_32_1_bus_0_2), .col1(square_32_1_bus_0_3), .col2(square_32_1_bus_0_4),
    .col3(square_32_1_bus_0_5));
  square_32 square_32_1 (
    .bus_0(32'h72707171), .bus_0_2(square_32_1_bus_0_2), .bus_0_3(square_32_1_bus_0_3),
    .bus_0_4(square_32_1_bus_0_4), .bus_0_5(square_32_1_bus_0_5));
  square_32 square_32_2 (
    .bus_0(32'h27270717), .bus_0_2(square_32_2_bus_0_2), .bus_0_3(square_32_2_bus_0_3),
    .bus_0_4(square_32_2_bus_0_4), .bus_0_5(square_32_2_bus_0_5));
  DotMatrix #(.matrixcols(4), .matrixrows(32)) dotmatrix_3 (
    .col0(square_32_3_bus_0_2), .col1(square_32_3_bus_0_3), .col2(square_32_3_bus_0_4),
    .col3(square_32_3_bus_0_5));
  DotMatrix #(.matrixcols(4), .matrixrows(32)) dotmatrix_4 (
    .col0(square_32_4_bus_0_2), .col1(square_32_4_bus_0_3), .col2(square_32_4_bus_0_4),
    .col3(square_32_4_bus_0_5));
  square_32 square_32_3 (
    .bus_0(32'h27270717), .bus_0_2(square_32_3_bus_0_2), .bus_0_3(square_32_3_bus_0_3),
    .bus_0_4(square_32_3_bus_0_4), .bus_0_5(square_32_3_bus_0_5));
  square_32 square_32_4 (
    .bus_0(32'h72707171), .bus_0_2(square_32_4_bus_0_2), .bus_0_3(square_32_4_bus_0_3),
    .bus_0_4(square_32_4_bus_0_4), .bus_0_5(square_32_4_bus_0_5));
  DotMatrix #(.matrixcols(4), .matrixrows(32)) dotmatrix_5 (
    .col0(square_32_5_bus_0_2), .col1(square_32_5_bus_0_3), .col2(square_32_5_bus_0_4),
    .col3(square_32_5_bus_0_5));
  DotMatrix #(.matrixcols(4), .matrixrows(32)) dotmatrix_6 (
    .col0(square_32_6_bus_0_2), .col1(square_32_6_bus_0_3), .col2(square_32_6_bus_0_4),
    .col3(square_32_6_bus_0_5));
  square_32 square_32_5 (
    .bus_0(32'h27270717), .bus_0_2(square_32_5_bus_0_2), .bus_0_3(square_32_5_bus_0_3),
    .bus_0_4(square_32_5_bus_0_4), .bus_0_5(square_32_5_bus_0_5));
  square_32 square_32_6 (
    .bus_0(32'h72707171), .bus_0_2(square_32_6_bus_0_2), .bus_0_3(square_32_6_bus_0_3),
    .bus_0_4(square_32_6_bus_0_4), .bus_0_5(square_32_6_bus_0_5));
  Register #(.width(4)) register_1 (.D(bit_extender_1_out), .en(act_0), .Q(register_1_q), .clk(act_0));  // open: clr
  Register #(.width(4)) register_2 (.D(bit_extender_1_out), .en(act_1), .Q(register_2_q), .clk(act_1));  // open: clr
  Register #(.width(4)) register_3 (.D(bit_extender_1_out), .en(act_2), .Q(register_3_q), .clk(act_2));  // open: clr
  Register #(.width(4)) register_4 (.D(bit_extender_1_out), .en(act_3), .Q(register_4_q), .clk(act_3));  // open: clr
  Register #(.width(4)) register_5 (.D(bit_extender_1_out), .en(act_4), .Q(register_5_q), .clk(act_4));  // open: clr
  Register #(.width(4)) register_6 (.D(bit_extender_1_out), .en(act_5), .Q(register_6_q), .clk(act_5));  // open: clr
  Register #(.width(4)) register_7 (.D(bit_extender_1_out), .en(act_6), .Q(register_7_q), .clk(act_6));  // open: clr
  Register #(.width(4)) register_8 (.D(bit_extender_1_out), .en(act_7), .Q(register_8_q), .clk(act_7));  // open: clr
  DotMatrix #(.matrixcols(4), .matrixrows(32)) dotmatrix_7 (
    .col0(square_32_8_bus_0_2), .col1(square_32_8_bus_0_3), .col2(square_32_8_bus_0_4),
    .col3(square_32_8_bus_0_5));
  DotMatrix #(.matrixcols(4), .matrixrows(32)) dotmatrix_8 (
    .col0(square_32_7_bus_0_2), .col1(square_32_7_bus_0_3), .col2(square_32_7_bus_0_4),
    .col3(square_32_7_bus_0_5));
  square_32 square_32_7 (
    .bus_0(32'h72707171), .bus_0_2(square_32_7_bus_0_2), .bus_0_3(square_32_7_bus_0_3),
    .bus_0_4(square_32_7_bus_0_4), .bus_0_5(square_32_7_bus_0_5));
  square_32 square_32_8 (
    .bus_0(32'h27270717), .bus_0_2(square_32_8_bus_0_2), .bus_0_3(square_32_8_bus_0_3),
    .bus_0_4(square_32_8_bus_0_4), .bus_0_5(square_32_8_bus_0_5));
  Comparator #(.width(6), .mode("unsigned")) comparator_4 (
    .a(address_bus[6:1]), .b({6{1'b0}}), .eq(comparator_4_eq));  // open: gt, lt
  Comparator #(.width(6), .mode("unsigned")) comparator_5 (
    .a(address_bus[6:1]), .b(6'b000001), .eq(comparator_5_eq));  // open: gt, lt
  Comparator #(.width(6), .mode("unsigned")) comparator_6 (
    .a(address_bus[6:1]), .b(6'b000010), .eq(comparator_6_eq));  // open: gt, lt
  Comparator #(.width(6), .mode("unsigned")) comparator_7 (
    .a(address_bus[6:1]), .b(6'b000011), .eq(comparator_7_eq));  // open: gt, lt
  and and_5 (act_0, is_board, comparator_4_eq);
  and and_6 (act_1, is_board, comparator_5_eq);
  and and_7 (act_2, is_board, comparator_6_eq);
  and and_8 (act_3, is_board, comparator_7_eq);
  DotMatrix #(.matrixcols(4), .matrixrows(32)) dotmatrix_9 (
    .col0(square_32_9_bus_0_2), .col1(square_32_9_bus_0_3), .col2(square_32_9_bus_0_4),
    .col3(square_32_9_bus_0_5));
  square_32 square_32_9 (
    .bus_0(\ооо_1_bus_0 ), .bus_0_2(square_32_9_bus_0_2), .bus_0_3(square_32_9_bus_0_3),
    .bus_0_4(square_32_9_bus_0_4), .bus_0_5(square_32_9_bus_0_5));
  \ооо  \u_ооо_1  (
    .bus_0(\ооо_1_bus_0 ), .in_1(register_1_q), .in_2(register_2_q), .in_3(register_3_q),
    .in_4(register_4_q), .in_5(register_5_q), .in_6(register_6_q), .in_7(register_7_q), .in_8(register_8_q));
  Comparator #(.width(6), .mode("unsigned")) comparator_8 (
    .a(address_bus[6:1]), .b(6'b000100), .eq(comparator_8_eq));  // open: gt, lt
  Comparator #(.width(6), .mode("unsigned")) comparator_9 (
    .a(address_bus[6:1]), .b(6'b000101), .eq(comparator_9_eq));  // open: gt, lt
  Comparator #(.width(6), .mode("unsigned")) comparator_10 (
    .a(address_bus[6:1]), .b(6'b000110), .eq(comparator_10_eq));  // open: gt, lt
  Comparator #(.width(6), .mode("unsigned")) comparator_11 (
    .a(address_bus[6:1]), .b(6'b000111), .eq(comparator_11_eq));  // open: gt, lt
  and and_9 (act_4, is_board, comparator_8_eq);
  and and_10 (act_5, is_board, comparator_9_eq);
  and and_11 (act_6, is_board, comparator_10_eq);
  and and_12 (act_7, is_board, comparator_11_eq);

  // Other names for the same wires on the sheet: low_bit[5:0] = address_bus[6:1]; high_bit[8:0] = address_bus[15:7]
endmodule

module \ооо  (
  input  [3:0] in_1,
  input  [3:0] in_2,
  input  [3:0] in_3,
  input  [3:0] in_4,
  input  [3:0] in_5,
  input  [3:0] in_6,
  input  [3:0] in_7,
  input  [3:0] in_8,
  output [31:0] bus_0
);


  assign bus_0 = {in_1, in_2, in_3, in_4, in_5, in_6, in_7, in_8};
endmodule
