// Logisim project control_device_reworked_extra_button.circ as structural Verilog: 9 circuits, main circuit main
module main (
);

  wire _1__next_checker_out, _2__choose_this_checker_out, _3__up_right_out, _4__up_left_out,
       _5__down_right_out, _6__down_left_out, _7__finish_turn_out, and_1_out, and_2_out, board_active,
       cdm_16_1_p1, cdm_16_1_p2, cdm_16_1_p4, cdm_16_1_p5, cdm_16_1_p6, cdm_16_1_p7, cdm_16_1_p8,
       cdm_16_1_p9, checker_select_1_led1, checker_select_1_led2, checker_select_1_led3,
       checker_select_1_led4, checker_select_1_led5, checker_select_1_led6, checker_select_1_led7,
       checker_select_1_led8, checker_select_1_leda, checker_select_1_ledb, checker_select_1_ledc,
       checker_select_1_ledd, checker_select_1_lede, checker_select_1_ledf, checker_select_1_ledg,
       checker_select_1_ledh, clock, is_active, memory_select, nor_1_out, not_1_out, read;
  wire [6:0] new_gamepad_1_raw_state, new_gamepad_1_register_state;
  wire [7:0] game_status_1_leds;
  wire [15:0] adress_bus, data_bus, data_in, data_out, ram_1_p6, transistor_1_out;
  wire [31:0] screen_1_column_a, screen_1_column_b, screen_1_column_c, screen_1_column_d, screen_1_column_e,
       screen_1_column_f, screen_1_column_g, screen_1_column_h, square_32_1_bus_0_2, square_32_1_bus_0_3,
       square_32_1_bus_0_4, square_32_1_bus_0_5, square_32_2_bus_0_2, square_32_2_bus_0_3,
       square_32_2_bus_0_4, square_32_2_bus_0_5, square_32_3_bus_0_2, square_32_3_bus_0_3,
       square_32_3_bus_0_4, square_32_3_bus_0_5, square_32_4_bus_0_2, square_32_4_bus_0_3,
       square_32_4_bus_0_4, square_32_4_bus_0_5, square_32_5_bus_0_2, square_32_5_bus_0_3,
       square_32_5_bus_0_4, square_32_5_bus_0_5, square_32_6_bus_0_2, square_32_6_bus_0_3,
       square_32_6_bus_0_4, square_32_6_bus_0_5, square_32_7_bus_0_2, square_32_7_bus_0_3,
       square_32_7_bus_0_4, square_32_7_bus_0_5, square_32_8_bus_0_2, square_32_8_bus_0_3,
       square_32_8_bus_0_4, square_32_8_bus_0_5;

  // Probe on adress_bus
  // Probe on data_bus
  // Probe on cdm_16_1_p9
  // Probe on cdm_16_1_p8
  // Probe on cdm_16_1_p7
  Clock clock_1 (.out(clock));
  checker_select checker_select_1 (
    .clock(clock), .data(data_bus), .adress(adress_bus), .led1(checker_select_1_led1),
    .leda(checker_select_1_leda), .led2(checker_select_1_led2), .ledb(checker_select_1_ledb),
    .led3(checker_select_1_led3), .ledc(checker_select_1_ledc), .led4(checker_select_1_led4),
    .ledd(checker_select_1_ledd), .led5(checker_select_1_led5), .lede(checker_select_1_lede),
    .led6(checker_select_1_led6), .ledf(checker_select_1_ledf), .led7(checker_select_1_led7),
    .ledg(checker_select_1_ledg), .led8(checker_select_1_led8), .ledh(checker_select_1_ledh),
    .read_write_prime(read), .memory_select(memory_select));
  not nor_1 (nor_1_out, is_active);  // NOR_Gate
  LED led_1 (.in(checker_select_1_ledb));
  LED led_2 (.in(checker_select_1_leda));
  DotMatrix #(.matrixcols(4), .matrixrows(32)) dotmatrix_1 (
    .col0(square_32_2_bus_0_2), .col1(square_32_2_bus_0_3), .col2(square_32_2_bus_0_4),
    .col3(square_32_2_bus_0_5));
  DotMatrix #(.matrixcols(4), .matrixrows(32)) dotmatrix_2 (
    .col0(square_32_1_bus_0_2), .col1(square_32_1_bus_0_3), .col2(square_32_1_bus_0_4),
    .col3(square_32_1_bus_0_5));
  square_32 square_32_1 (
    .bus_0(screen_1_column_a), .bus_0_2(square_32_1_bus_0_2), .bus_0_3(square_32_1_bus_0_3),
    .bus_0_4(square_32_1_bus_0_4), .bus_0_5(square_32_1_bus_0_5));
  square_32 square_32_2 (
    .bus_0(screen_1_column_b), .bus_0_2(square_32_2_bus_0_2), .bus_0_3(square_32_2_bus_0_3),
    .bus_0_4(square_32_2_bus_0_4), .bus_0_5(square_32_2_bus_0_5));
  // Probe on cdm_16_1_p6
  // Probe on cdm_16_1_p5
  // Probe on cdm_16_1_p4
  // Probe on cdm_16_1_p2
  // Probe on cdm_16_1_p1
  // CdM_16 cdm_16_1: pin names not known; wires that end beside it: cdm_16_1_p1, cdm_16_1_p2, clock, cdm_16_1_p4, cdm_16_1_p5, cdm_16_1_p6, cdm_16_1_p7, cdm_16_1_p8, cdm_16_1_p9, memory_select, read, adress_bus, data_out, data_in
  LED led_3 (.in(checker_select_1_ledc));
  LED led_4 (.in(checker_select_1_ledd));
  DotMatrix #(.matrixcols(4), .matrixrows(32)) dotmatrix_3 (
    .col0(square_32_4_bus_0_2), .col1(square_32_4_bus_0_3), .col2(square_32_4_bus_0_4),
    .col3(square_32_4_bus_0_5));
  DotMatrix #(.matrixcols(4), .matrixrows(32)) dotmatrix_4 (
    .col0(square_32_3_bus_0_2), .col1(square_32_3_bus_0_3), .col2(square_32_3_bus_0_4),
    .col3(square_32_3_bus_0_5));
  square_32 square_32_3 (
    .bus_0(screen_1_column_d), .bus_0_2(square_32_3_bus_0_2), .bus_0_3(square_32_3_bus_0_3),
    .bus_0_4(square_32_3_bus_0_4), .bus_0_5(square_32_3_bus_0_5));
  square_32 square_32_4 (
    .bus_0(screen_1_column_c), .bus_0_2(square_32_4_bus_0_2), .bus_0_3(square_32_4_bus_0_3),
    .bus_0_4(square_32_4_bus_0_4), .bus_0_5(square_32_4_bus_0_5));
  LED led_5 (.in(checker_select_1_lede));
  LED led_6 (.in(checker_select_1_ledf));
  DotMatrix #(.matrixcols(4), .matrixrows(32)) dotmatrix_5 (
    .col0(square_32_5_bus_0_2), .col1(square_32_5_bus_0_3), .col2(square_32_5_bus_0_4),
    .col3(square_32_5_bus_0_5));
  DotMatrix #(.matrixcols(4), .matrixrows(32)) dotmatrix_6 (
    .col0(square_32_6_bus_0_2), .col1(square_32_6_bus_0_3), .col2(square_32_6_bus_0_4),
    .col3(square_32_6_bus_0_5));
  square_32 square_32_5 (
    .bus_0(screen_1_column_e), .bus_0_2(square_32_5_bus_0_2), .bus_0_3(square_32_5_bus_0_3),
    .bus_0_4(square_32_5_bus_0_4), .bus_0_5(square_32_5_bus_0_5));
  square_32 square_32_6 (
    .bus_0(screen_1_column_f), .bus_0_2(square_32_6_bus_0_2), .bus_0_3(square_32_6_bus_0_3),
    .bus_0_4(square_32_6_bus_0_4), .bus_0_5(square_32_6_bus_0_5));
  screen screen_1 (
    .clock(clock), .read(read), .adress(adress_bus), .data(data_bus), .column_d(screen_1_column_d),
    .column_h(screen_1_column_h), .column_c(screen_1_column_c), .column_g(screen_1_column_g),
    .column_b(screen_1_column_b), .column_f(screen_1_column_f), .column_a(screen_1_column_a),
    .column_e(screen_1_column_e), .active(board_active), .memory_select(memory_select));
  Transistor #(.\type ("n"), .width(16)) transistor_1 (.in(data_out), .out(transistor_1_out), .gate(nor_1_out));
  assign data_bus = not_1_out ? transistor_1_out : 16'bz;  // Controlled_Buffer controlled_buffer_1
  not not_1 (not_1_out, read);
  assign data_in = read ? data_bus : 16'bz;  // Controlled_Buffer controlled_buffer_2
  LED led_7 (.in(checker_select_1_ledg));
  LED led_8 (.in(checker_select_1_ledh));
  DotMatrix #(.matrixcols(4), .matrixrows(32)) dotmatrix_7 (
    .col0(square_32_7_bus_0_2), .col1(square_32_7_bus_0_3), .col2(square_32_7_bus_0_4),
    .col3(square_32_7_bus_0_5));
  DotMatrix #(.matrixcols(4), .matrixrows(32)) dotmatrix_8 (
    .col0(square_32_8_bus_0_2), .col1(square_32_8_bus_0_3), .col2(square_32_8_bus_0_4),
    .col3(square_32_8_bus_0_5));
  square_32 square_32_7 (
    .bus_0(screen_1_column_g), .bus_0_2(square_32_7_bus_0_2), .bus_0_3(square_32_7_bus_0_3),
    .bus_0_4(square_32_7_bus_0_4), .bus_0_5(square_32_7_bus_0_5));
  square_32 square_32_8 (
    .bus_0(screen_1_column_h), .bus_0_2(square_32_8_bus_0_2), .bus_0_3(square_32_8_bus_0_3),
    .bus_0_4(square_32_8_bus_0_4), .bus_0_5(square_32_8_bus_0_5));
  // RAM ram_1: pin names not known; wires that end beside it: adress_bus, 1'b1, memory_select, clock, read, ram_1_p6
  LED led_9 (.in(checker_select_1_led1));
  LED led_10 (.in(checker_select_1_led2));
  LED led_11 (.in(checker_select_1_led3));
  LED led_12 (.in(checker_select_1_led4));
  LED led_13 (.in(checker_select_1_led5));
  LED led_14 (.in(checker_select_1_led6));
  LED led_15 (.in(checker_select_1_led7));
  LED led_16 (.in(checker_select_1_led8));
  and and_1 (and_1_out, read, ~is_active, ~board_active);  // AND_Gate
  assign data_bus = and_1_out ? ram_1_p6 : 16'bz;  // Controlled_Buffer controlled_buffer_3
  assign ram_1_p6 = and_2_out ? data_bus : 16'bz;  // Controlled_Buffer controlled_buffer_4
  and and_2 (and_2_out, ~read, ~is_active, ~board_active);  // AND_Gate
  // Probe on new_gamepad_1_register_state
  // Probe on new_gamepad_1_raw_state
  game_status game_status_1 (
    .clock(clock), .adress(adress_bus), .read(read), .data(data_bus), .leds(game_status_1_leds),
    .memory_select(memory_select));
  new_gamepad new_gamepad_1 (
    .checker_select(_1__next_checker_out), .clock(clock), .is_active(is_active), .left_up(_4__up_left_out),
    .adress_bus(adress_bus), .data(data_bus), .right_up(_3__up_right_out),
    .raw_state(new_gamepad_1_raw_state), .right_down(_5__down_right_out),
    .register_state(new_gamepad_1_register_state), .left_down(_6__down_left_out),
    .finnish_turn(_7__finish_turn_out), .end_choose_checker(_2__choose_this_checker_out));
  LED _1__INVALID_INPUT (.in(game_status_1_leds[1]));
  LED _2__YOUR_TURN__CHOOSE_CHECKER (.in(game_status_1_leds[2]));
  LED _3__YOUR_TURN__CHOOSE_DIRECTION (.in(game_status_1_leds[3]));
  LED _4__OPPONENT_S_TURN (.in(game_status_1_leds[4]));
  LED _5__YOU_WON (.in(game_status_1_leds[5]));
  LED _6__YOU_LOST (.in(game_status_1_leds[6]));
  LED _7__DRAW (.in(game_status_1_leds[7]));
  Button _1__next_checker (.out(_1__next_checker_out));
  Button _4__up_left (.out(_4__up_left_out));
  Button _6__down_left (.out(_6__down_left_out));
  Button _2__choose_this_checker (.out(_2__choose_this_checker_out));
  Button _3__up_right (.out(_3__up_right_out));
  Button _5__down_right (.out(_5__down_right_out));
  Button _7__finish_turn (.out(_7__finish_turn_out));

  // Notes on the sheet:
  //   блокировка процессора
  //   блокировка памяти
endmodule

module new_gamepad (
  input  checker_select,
  input  clock,
  input  end_choose_checker,
  input  [15:0] adress_bus,
  input  left_up,
  input  right_up,
  input  right_down,
  input  left_down,
  input  finnish_turn,
  output is_active,
  output [15:0] data,
  output [6:0] raw_state,
  output [6:0] register_state
);

  wire d_ff_1_q, d_ff_2_q, d_ff_3_q, d_ff_4_q, d_ff_5_q, d_ff_6_q, d_ff_7_q, d_ff_8_q, d_ff_9_q, d_ff_10_q,
       d_ff_11_q, d_ff_12_q, d_ff_13_q, d_ff_14_q, not_1_out, register_1_q, register_2_q, register_3_q,
       register_5_q, register_6_q, register_7_q, register_8_q, register_9_q, register_10_q, reset1, reset2;
  wire [15:15] pull_resistor_1_node;

  Register #(.width(1)) register_1 (.D(is_active), .Q(register_1_q), .clk(clock));  // open: en, clr
  D_Flip_Flop d_ff_1 (.clk(left_up), .D(1'b1), .Q(d_ff_1_q), .reset(reset1));  // open: Qn, preset, en
  D_Flip_Flop d_ff_2 (.clk(left_up), .D(1'b1), .Q(d_ff_2_q), .reset(reset2));  // open: Qn, preset, en
  D_Flip_Flop d_ff_3 (.clk(left_down), .D(1'b1), .Q(d_ff_3_q), .reset(reset1));  // open: Qn, preset, en
  D_Flip_Flop d_ff_4 (.clk(left_down), .D(1'b1), .Q(d_ff_4_q), .reset(reset2));  // open: Qn, preset, en
  Register #(.width(1)) register_2 (.D(register_1_q), .Q(register_2_q), .clk(clock));  // open: en, clr
  or or_1 (raw_state[3], d_ff_1_q, d_ff_2_q);
  or or_2 (raw_state[5], d_ff_3_q, d_ff_4_q);
  Register #(.width(1)) register_3 (.D(register_2_q), .Q(register_3_q), .clk(clock));  // open: en, clr
  Register #(.width(1)) register_4 (.D(register_3_q), .Q(reset1), .clk(clock));  // open: en, clr
  D_Flip_Flop d_ff_5 (.clk(right_up), .D(1'b1), .Q(d_ff_5_q), .reset(reset1));  // open: Qn, preset, en
  D_Flip_Flop d_ff_6 (.clk(right_up), .D(1'b1), .Q(d_ff_6_q), .reset(reset2));  // open: Qn, preset, en
  D_Flip_Flop d_ff_7 (.clk(right_down), .D(1'b1), .Q(d_ff_7_q), .reset(reset1));  // open: Qn, preset, en
  D_Flip_Flop d_ff_8 (.clk(right_down), .D(1'b1), .Q(d_ff_8_q), .reset(reset2));  // open: Qn, preset, en
  D_Flip_Flop d_ff_9 (.clk(end_choose_checker), .D(1'b1), .Q(d_ff_9_q), .reset(reset1));  // open: Qn, preset, en
  D_Flip_Flop d_ff_10 (.clk(end_choose_checker), .D(1'b1), .Q(d_ff_10_q), .reset(reset2));  // open: Qn, preset, en
  Register #(.width(1)) register_5 (.D(reset1), .Q(register_5_q), .clk(clock));  // open: en, clr
  Register #(.width(1)) register_6 (.D(register_5_q), .Q(register_6_q), .clk(clock));  // open: en, clr
  or or_3 (raw_state[2], d_ff_5_q, d_ff_6_q);
  or or_4 (raw_state[4], d_ff_7_q, d_ff_8_q);
  or or_5 (raw_state[1], d_ff_9_q, d_ff_10_q);
  Register #(.width(1)) register_7 (.D(register_6_q), .Q(register_7_q), .clk(clock));  // open: en, clr
  D_Flip_Flop d_ff_11 (.clk(checker_select), .D(1'b1), .Q(d_ff_11_q), .reset(reset1));  // open: Qn, preset, en
  D_Flip_Flop d_ff_12 (.clk(checker_select), .D(1'b1), .Q(d_ff_12_q), .reset(reset2));  // open: Qn, preset, en
  D_Flip_Flop d_ff_13 (.clk(finnish_turn), .D(1'b1), .Q(d_ff_13_q), .reset(reset1));  // open: Qn, preset, en
  D_Flip_Flop d_ff_14 (.clk(finnish_turn), .D(1'b1), .Q(d_ff_14_q), .reset(reset2));  // open: Qn, preset, en
  Register #(.width(1)) register_8 (.D(register_7_q), .Q(register_8_q), .clk(clock));  // open: en, clr
  or or_6 (raw_state[0], d_ff_11_q, d_ff_12_q);
  or or_7 (raw_state[6], d_ff_13_q, d_ff_14_q);
  Register #(.width(1)) register_9 (.D(register_8_q), .Q(register_9_q), .clk(clock));  // open: en, clr
  Register #(.width(1)) register_10 (.D(register_9_q), .Q(register_10_q), .clk(clock));  // open: en, clr
  // Probe on register_state
  Register #(.width(7)) register_11 (.D(raw_state), .en(1'b1), .Q(register_state), .clk(clock));  // open: clr
  Register #(.width(1)) register_12 (.D(register_10_q), .Q(reset2), .clk(clock));  // open: en, clr
  Pull_Resistor pull_resistor_1 (.node(pull_resistor_1_node[15]));
  not not_1 (not_1_out, adress_bus[0]);
  and and_1 (is_active, not_1_out, adress_bus[1], adress_bus[2], adress_bus[3], adress_bus[4], adress_bus[5], adress_bus[6], adress_bus[7], adress_bus[9], adress_bus[10], adress_bus[11], adress_bus[12], adress_bus[13], adress_bus[14], adress_bus[15], adress_bus[8]);
  assign data = is_active ? {{9{pull_resistor_1_node[15]}}, register_state} : 16'bz;  // Controlled_Buffer controlled_buffer_1

  // Other names for the same wires on the sheet: data_bus[15:0] = data; finish_turn = finnish_turn
endmodule

module checker_select (
  input  clock,
  input  read_write_prime,
  input  [15:0] data,
  input  memory_select,
  input  [15:0] adress,
  output led1,
  output led2,
  output led3,
  output led4,
  output led5,
  output led6,
  output led7,
  output led8,
  output leda,
  output ledb,
  output ledc,
  output ledd,
  output lede,
  output ledf,
  output ledg,
  output ledh
);

  wire enable;
  wire [2:0] register_1_q, register_2_q;

  and and_1 (enable, ~adress[0], ~adress[1], adress[2], adress[3], adress[4], adress[5], adress[6], adress[7], adress[8], adress[10], adress[11], adress[12], adress[13], adress[14], adress[9], adress[15], ~read_write_prime, memory_select);  // AND_Gate
  Register #(.width(3)) register_1 (.D(data[5:3]), .en(enable), .Q(register_1_q), .clk(clock), .clr(1'b0));
  Decoder #(.select(3)) decoder_1 (
    .out0(leda), .out1(ledb), .out2(ledc), .out3(ledd), .out4(lede), .out5(ledf), .out6(ledg), .out7(ledh),
    .sel(register_1_q));  // open: en
  Decoder #(.select(3)) decoder_2 (
    .out0(led1), .out1(led2), .out2(led3), .out3(led4), .out4(led5), .out5(led6), .out6(led7), .out7(led8),
    .sel(register_2_q));  // open: en
  Register #(.width(3)) register_2 (.D(data[2:0]), .en(enable), .Q(register_2_q), .clk(clock), .clr(1'b0));
endmodule

module game_status (
  input  clock,
  input  [15:0] adress,
  input  read,
  input  [15:0] data,
  input  memory_select,
  output [7:0] leds
);

  wire is_active;
  wire [7:0] decoder_1_out0;

  and and_1 (is_active, ~adress[0], adress[1], ~adress[2], adress[3], adress[4], adress[5], adress[6], adress[7], adress[8], adress[10], adress[11], adress[12], adress[13], adress[14], adress[15], adress[9], ~read, memory_select);  // AND_Gate
  Decoder #(.select(3)) decoder_1 (
    .out0(decoder_1_out0[0]), .out1(decoder_1_out0[1]), .out2(decoder_1_out0[2]), .out3(decoder_1_out0[3]),
    .out4(decoder_1_out0[4]), .out5(decoder_1_out0[5]), .out6(decoder_1_out0[6]), .out7(decoder_1_out0[7]),
    .sel(data[2:0]), .en(is_active));
  Register register_1 (.D(decoder_1_out0), .en(is_active), .Q(leds), .clk(clock));  // open: clr
  // Probe on leds
endmodule

module screen (
  input  clock,
  input  read,
  input  [15:0] adress,
  input  [15:0] data,
  input  memory_select,
  output [31:0] column_d,
  output [31:0] column_c,
  output [31:0] column_b,
  output [31:0] column_a,
  output [31:0] column_h,
  output [31:0] column_g,
  output [31:0] column_f,
  output [31:0] column_e,
  output active
);

  wire _0, _1, _2, _3, _4, _5, _6, _7, _8, _9, _10, _11, _12, _13, _14, _15, _16, _17, _18, _19, _20, _21,
       _22, _23, _24, _25, _26, _27, _28, _29, _30, _31, and_1_out, and_2_out;
  wire [31:0] square_32_1_bus_0_2, square_32_1_bus_0_3, square_32_1_bus_0_4, square_32_1_bus_0_5,
       square_32_2_bus_0_2, square_32_2_bus_0_3, square_32_2_bus_0_4, square_32_2_bus_0_5,
       square_32_3_bus_0_2, square_32_3_bus_0_3, square_32_3_bus_0_4, square_32_3_bus_0_5,
       square_32_4_bus_0_2, square_32_4_bus_0_3, square_32_4_bus_0_4, square_32_4_bus_0_5,
       square_32_5_bus_0_2, square_32_5_bus_0_3, square_32_5_bus_0_4, square_32_5_bus_0_5,
       square_32_6_bus_0_2, square_32_6_bus_0_3, square_32_6_bus_0_4, square_32_6_bus_0_5,
       square_32_7_bus_0_2, square_32_7_bus_0_3, square_32_7_bus_0_4, square_32_7_bus_0_5,
       square_32_8_bus_0_2, square_32_8_bus_0_3, square_32_8_bus_0_4, square_32_8_bus_0_5;

  Decoder #(.select(5)) decoder_1 (
    .out0(_0), .out1(_1), .out2(_2), .out3(_3), .out4(_4), .out5(_5), .out6(_6), .out7(_7), .out8(_8),
    .out9(_9), .out10(_10), .out11(_11), .out12(_12), .out13(_13), .out14(_14), .out15(_15), .out16(_16),
    .out17(_17), .out18(_18), .out19(_19), .out20(_20), .out21(_21), .out22(_22), .out23(_23), .out24(_24),
    .out25(_25), .out26(_26), .out27(_27), .out28(_28), .out29(_29), .out30(_30), .out31(_31),
    .sel(adress[5:1]));  // open: en
  and and_1 (and_1_out, ~data[4], ~data[5], ~data[6], ~data[7], ~data[8], ~data[9], ~data[11], ~data[12], ~data[13], ~data[14], ~data[15], ~data[10]);  // AND_Gate
  \cell  cell_1 (.clock(clock), .activate(active), .cell_state(column_h[7:4]), .postfix_data(data[3:0]), .tag(_0));
  \cell  cell_2 (.clock(clock), .activate(active), .cell_state(column_h[15:12]), .postfix_data(data[3:0]), .tag(_1));
  \cell  cell_3 (.clock(clock), .activate(active), .cell_state(column_h[23:20]), .postfix_data(data[3:0]), .tag(_2));
  \cell  cell_4 (.clock(clock), .activate(active), .cell_state(column_h[31:28]), .postfix_data(data[3:0]), .tag(_3));
  \cell  cell_5 (.clock(clock), .activate(active), .cell_state(column_g[3:0]), .postfix_data(data[3:0]), .tag(_4));
  \cell  cell_6 (.clock(clock), .activate(active), .cell_state(column_g[11:8]), .postfix_data(data[3:0]), .tag(_5));
  \cell  cell_7 (.clock(clock), .activate(active), .cell_state(column_g[19:16]), .postfix_data(data[3:0]), .tag(_6));
  \cell  cell_8 (.clock(clock), .activate(active), .cell_state(column_g[27:24]), .postfix_data(data[3:0]), .tag(_7));
  and and_2 (and_2_out, ~adress[0], ~read, ~adress[6], adress[9], adress[7], adress[8], adress[10], adress[11], adress[12], adress[13], adress[14], adress[15]);  // AND_Gate
  and and_3 (active, and_1_out, memory_select, and_2_out);
  \cell  cell_9 (.clock(clock), .activate(active), .cell_state(column_f[7:4]), .postfix_data(data[3:0]), .tag(_8));
  \cell  cell_10 (.clock(clock), .activate(active), .cell_state(column_f[15:12]), .postfix_data(data[3:0]), .tag(_9));
  \cell  cell_11 (.clock(clock), .activate(active), .cell_state(column_f[23:20]), .postfix_data(data[3:0]), .tag(_10));
  \cell  cell_12 (.clock(clock), .activate(active), .cell_state(column_f[31:28]), .postfix_data(data[3:0]), .tag(_11));
  \cell  cell_13 (.clock(clock), .activate(active), .cell_state(column_e[3:0]), .postfix_data(data[3:0]), .tag(_12));
  \cell  cell_14 (.clock(clock), .activate(active), .cell_state(column_e[11:8]), .postfix_data(data[3:0]), .tag(_13));
  \cell  cell_15 (.clock(clock), .activate(active), .cell_state(column_e[19:16]), .postfix_data(data[3:0]), .tag(_14));
  \cell  cell_16 (.clock(clock), .activate(active), .cell_state(column_e[27:24]), .postfix_data(data[3:0]), .tag(_15));
  \cell  cell_17 (.clock(clock), .activate(active), .cell_state(column_d[7:4]), .postfix_data(data[3:0]), .tag(_16));
  \cell  cell_18 (.clock(clock), .activate(active), .cell_state(column_d[15:12]), .postfix_data(data[3:0]), .tag(_17));
  \cell  cell_19 (.clock(clock), .activate(active), .cell_state(column_d[23:20]), .postfix_data(data[3:0]), .tag(_18));
  \cell  cell_20 (.clock(clock), .activate(active), .cell_state(column_d[31:28]), .postfix_data(data[3:0]), .tag(_19));
  \cell  cell_21 (.clock(clock), .activate(active), .cell_state(column_c[3:0]), .postfix_data(data[3:0]), .tag(_20));
  \cell  cell_22 (.clock(clock), .activate(active), .cell_state(column_c[11:8]), .postfix_data(data[3:0]), .tag(_21));
  \cell  cell_23 (.clock(clock), .activate(active), .cell_state(column_c[19:16]), .postfix_data(data[3:0]), .tag(_22));
  \cell  cell_24 (.clock(clock), .activate(active), .cell_state(column_c[27:24]), .postfix_data(data[3:0]), .tag(_23));
  DotMatrix #(.matrixcols(4), .matrixrows(32)) dotmatrix_1 (
    .col0(square_32_1_bus_0_2), .col1(square_32_1_bus_0_3), .col2(square_32_1_bus_0_4),
    .col3(square_32_1_bus_0_5));
  DotMatrix #(.matrixcols(4), .matrixrows(32)) dotmatrix_2 (
    .col0(square_32_2_bus_0_2), .col1(square_32_2_bus_0_3), .col2(square_32_2_bus_0_4),
    .col3(square_32_2_bus_0_5));
  square_32 square_32_1 (
    .bus_0({column_b[31:28], 4'b1110, column_b[23:20], 4'b1110, column_b[15:12], 4'b1110, column_b[7:4], 4'b1110}),
    .bus_0_2(square_32_1_bus_0_2), .bus_0_3(square_32_1_bus_0_3), .bus_0_4(square_32_1_bus_0_4),
    .bus_0_5(square_32_1_bus_0_5));
  square_32 square_32_2 (
    .bus_0({4'b1110, column_a[27:24], 4'b1110, column_a[19:16], 4'b1110, column_a[11:8], 4'b1110, column_a[3:0]}),
    .bus_0_2(square_32_2_bus_0_2), .bus_0_3(square_32_2_bus_0_3), .bus_0_4(square_32_2_bus_0_4),
    .bus_0_5(square_32_2_bus_0_5));
  DotMatrix #(.matrixcols(4), .matrixrows(32)) dotmatrix_3 (
    .col0(square_32_3_bus_0_2), .col1(square_32_3_bus_0_3), .col2(square_32_3_bus_0_4),
    .col3(square_32_3_bus_0_5));
  DotMatrix #(.matrixcols(4), .matrixrows(32)) dotmatrix_4 (
    .col0(square_32_4_bus_0_2), .col1(square_32_4_bus_0_3), .col2(square_32_4_bus_0_4),
    .col3(square_32_4_bus_0_5));
  square_32 square_32_3 (
    .bus_0({4'b1110, column_c[27:24], 4'b1110, column_c[19:16], 4'b1110, column_c[11:8], 4'b1110, column_c[3:0]}),
    .bus_0_2(square_32_3_bus_0_2), .bus_0_3(square_32_3_bus_0_3), .bus_0_4(square_32_3_bus_0_4),
    .bus_0_5(square_32_3_bus_0_5));
  square_32 square_32_4 (
    .bus_0({column_d[31:28], 4'b1110, column_d[23:20], 4'b1110, column_d[15:12], 4'b1110, column_d[7:4], 4'b1110}),
    .bus_0_2(square_32_4_bus_0_2), .bus_0_3(square_32_4_bus_0_3), .bus_0_4(square_32_4_bus_0_4),
    .bus_0_5(square_32_4_bus_0_5));
  DotMatrix #(.matrixcols(4), .matrixrows(32)) dotmatrix_5 (
    .col0(square_32_5_bus_0_2), .col1(square_32_5_bus_0_3), .col2(square_32_5_bus_0_4),
    .col3(square_32_5_bus_0_5));
  DotMatrix #(.matrixcols(4), .matrixrows(32)) dotmatrix_6 (
    .col0(square_32_6_bus_0_2), .col1(square_32_6_bus_0_3), .col2(square_32_6_bus_0_4),
    .col3(square_32_6_bus_0_5));
  square_32 square_32_5 (
    .bus_0({column_f[31:28], 4'b1110, column_f[23:20], 4'b1110, column_f[15:12], 4'b1110, column_f[7:4], 4'b1110}),
    .bus_0_2(square_32_5_bus_0_2), .bus_0_3(square_32_5_bus_0_3), .bus_0_4(square_32_5_bus_0_4),
    .bus_0_5(square_32_5_bus_0_5));
  square_32 square_32_6 (
    .bus_0({4'b1110, column_e[27:24], 4'b1110, column_e[19:16], 4'b1110, column_e[11:8], 4'b1110, column_e[3:0]}),
    .bus_0_2(square_32_6_bus_0_2), .bus_0_3(square_32_6_bus_0_3), .bus_0_4(square_32_6_bus_0_4),
    .bus_0_5(square_32_6_bus_0_5));
  \cell  cell_25 (.clock(clock), .activate(active), .cell_state(column_b[7:4]), .postfix_data(data[3:0]), .tag(_24));
  \cell  cell_26 (.clock(clock), .activate(active), .cell_state(column_b[15:12]), .postfix_data(data[3:0]), .tag(_25));
  \cell  cell_27 (.clock(clock), .activate(active), .cell_state(column_b[23:20]), .postfix_data(data[3:0]), .tag(_26));
  \cell  cell_28 (.clock(clock), .activate(active), .cell_state(column_b[31:28]), .postfix_data(data[3:0]), .tag(_27));
  \cell  cell_29 (.clock(clock), .activate(active), .cell_state(column_a[3:0]), .postfix_data(data[3:0]), .tag(_28));
  \cell  cell_30 (.clock(clock), .activate(active), .cell_state(column_a[11:8]), .postfix_data(data[3:0]), .tag(_29));
  \cell  cell_31 (.clock(clock), .activate(active), .cell_state(column_a[19:16]), .postfix_data(data[3:0]), .tag(_30));
  \cell  cell_32 (.clock(clock), .activate(active), .cell_state(column_a[27:24]), .postfix_data(data[3:0]), .tag(_31));
  DotMatrix #(.matrixcols(4), .matrixrows(32)) dotmatrix_7 (
    .col0(square_32_8_bus_0_2), .col1(square_32_8_bus_0_3), .col2(square_32_8_bus_0_4),
    .col3(square_32_8_bus_0_5));
  DotMatrix #(.matrixcols(4), .matrixrows(32)) dotmatrix_8 (
    .col0(square_32_7_bus_0_2), .col1(square_32_7_bus_0_3), .col2(square_32_7_bus_0_4),
    .col3(square_32_7_bus_0_5));
  square_32 square_32_7 (
    .bus_0({4'b1110, column_g[27:24], 4'b1110, column_g[19:16], 4'b1110, column_g[11:8], 4'b1110, column_g[3:0]}),
    .bus_0_2(square_32_7_bus_0_2), .bus_0_3(square_32_7_bus_0_3), .bus_0_4(square_32_7_bus_0_4),
    .bus_0_5(square_32_7_bus_0_5));
  square_32 square_32_8 (
    .bus_0({column_h[31:28], 4'b1110, column_h[23:20], 4'b1110, column_h[15:12], 4'b1110, column_h[7:4], 4'b1110}),
    .bus_0_2(square_32_8_bus_0_2), .bus_0_3(square_32_8_bus_0_3), .bus_0_4(square_32_8_bus_0_4),
    .bus_0_5(square_32_8_bus_0_5));

  assign {column_a[31:28], column_a[23:20], column_a[15:12], column_a[7:4]} = 16'heeee;
  assign {column_b[27:24], column_b[19:16], column_b[11:8], column_b[3:0]} = 16'heeee;
  assign {column_c[31:28], column_c[23:20], column_c[15:12], column_c[7:4]} = 16'heeee;
  assign {column_d[27:24], column_d[19:16], column_d[11:8], column_d[3:0]} = 16'heeee;
  assign {column_e[31:28], column_e[23:20], column_e[15:12], column_e[7:4]} = 16'heeee;
  assign {column_f[27:24], column_f[19:16], column_f[11:8], column_f[3:0]} = 16'heeee;
  assign {column_g[31:28], column_g[23:20], column_g[15:12], column_g[7:4]} = 16'heeee;
  assign {column_h[27:24], column_h[19:16], column_h[11:8], column_h[3:0]} = 16'heeee;

  // Other names for the same wires on the sheet: activate = active;
  //   columna (some bits) = {column_a[27:24], column_a[19:16], column_a[11:8], column_a[3:0]};
  //   columnb (some bits) = {column_b[31:28], column_b[23:20], column_b[15:12], column_b[7:4]};
  //   columnc (some bits) = {column_c[27:24], column_c[19:16], column_c[11:8], column_c[3:0]};
  //   columnd (some bits) = {column_d[31:28], column_d[23:20], column_d[15:12], column_d[7:4]};
  //   columne (some bits) = {column_e[27:24], column_e[19:16], column_e[11:8], column_e[3:0]};
  //   columnf (some bits) = {column_f[31:28], column_f[23:20], column_f[15:12], column_f[7:4]};
  //   columng (some bits) = {column_g[27:24], column_g[19:16], column_g[11:8], column_g[3:0]};
  //   columnh (some bits) = {column_h[31:28], column_h[23:20], column_h[15:12], column_h[7:4]};
  //   data_postfix[3:0] = data[3:0]

  // Notes on the sheet:
  //   0 - empty black cell
  //   7 - empty white cell
  //   1 - white checker
  //   2 - black checker
  //   3 - white king
  //   4 - black king
endmodule

module square (
  input  [3:0] number0_4,
  output [3:0] bus_0,
  output [3:0] bus_1,
  output [3:0] bus_2,
  output [3:0] bus_3
);

  wire [1:1] type_2;
  wire [2:0] bit_extender_1_out;
  wire [2:1] type_1;

  Bit_Extender #(.in_width(4), .out_width(3)) bit_extender_1 (.in(number0_4), .out(bit_extender_1_out));
  Multiplexer #(.select(3), .width(4)) multiplexer_1 (
    .in0(4'b0000), .in1(4'b0110), .in2({1'b0, type_1, 1'b0}), .in3(4'b0110), .in4({1'b0, type_1, 1'b0}),
    .in5(4'b1111), .in6(4'b1111), .in7(4'b1111), .out(bus_1), .sel(bit_extender_1_out));  // open: en
  // Probe on bus_1
  Multiplexer #(.select(3), .width(4)) multiplexer_2 (
    .in0(4'b0000), .in1(4'b0110), .in2({1'b0, type_1, 1'b0}), .in3(4'b0010), .in4({2'b00, type_2[1], 1'b0}),
    .in5(4'b1111), .in6(4'b1111), .in7(4'b1111), .out(bus_2), .sel(bit_extender_1_out));  // open: en
  Multiplexer #(.select(3), .width(4)) multiplexer_3 (
    .in0(4'b0000), .in1(4'b0000), .in2(4'b0000), .in3(4'b0000), .in4(4'b0000), .in5(4'b1111), .in6(4'b1111),
    .in7(4'b1111), .out(bus_0), .sel(bit_extender_1_out));  // open: en

  assign bus_3 = bus_0;
endmodule

module square_32 (
  input  [31:0] bus_0,
  output [31:0] bus_0_2,
  output [31:0] bus_0_3,
  output [31:0] bus_0_4,
  output [31:0] bus_0_5
);

  square square_1 (
    .number0_4(bus_0[3:0]), .bus_0(bus_0_2[3:0]), .bus_1(bus_0_3[3:0]), .bus_2(bus_0_4[3:0]),
    .bus_3(bus_0_5[3:0]));
  square square_2 (
    .number0_4(bus_0[7:4]), .bus_0(bus_0_2[7:4]), .bus_1(bus_0_3[7:4]), .bus_2(bus_0_4[7:4]),
    .bus_3(bus_0_5[7:4]));
  square square_3 (
    .number0_4(bus_0[11:8]), .bus_0(bus_0_2[11:8]), .bus_1(bus_0_3[11:8]), .bus_2(bus_0_4[11:8]),
    .bus_3(bus_0_5[11:8]));
  square square_4 (
    .number0_4(bus_0[15:12]), .bus_0(bus_0_2[15:12]), .bus_1(bus_0_3[15:12]), .bus_2(bus_0_4[15:12]),
    .bus_3(bus_0_5[15:12]));
  square square_5 (
    .number0_4(bus_0[19:16]), .bus_0(bus_0_2[19:16]), .bus_1(bus_0_3[19:16]), .bus_2(bus_0_4[19:16]),
    .bus_3(bus_0_5[19:16]));
  square square_6 (
    .number0_4(bus_0[23:20]), .bus_0(bus_0_2[23:20]), .bus_1(bus_0_3[23:20]), .bus_2(bus_0_4[23:20]),
    .bus_3(bus_0_5[23:20]));
  square square_7 (
    .number0_4(bus_0[27:24]), .bus_0(bus_0_2[27:24]), .bus_1(bus_0_3[27:24]), .bus_2(bus_0_4[27:24]),
    .bus_3(bus_0_5[27:24]));
  square square_8 (
    .number0_4(bus_0[31:28]), .bus_0(bus_0_2[31:28]), .bus_1(bus_0_3[31:28]), .bus_2(bus_0_4[31:28]),
    .bus_3(bus_0_5[31:28]));
endmodule

module \cell  (
  input  clock,
  input  activate,
  input  [3:0] postfix_data,
  input  tag,
  output [3:0] cell_state
);

  wire and_1_out, pull_resistor_1_node;

  and and_1 (and_1_out, activate, tag);
  Register #(.width(4)) register_1 (
    .D(postfix_data), .en(and_1_out), .Q(cell_state), .clk(clock), .clr(pull_resistor_1_node));
  Pull_Resistor pull_resistor_1 (.node(pull_resistor_1_node));
  // Probe on cell_state
endmodule

module gamepad (
  input  checker_select,
  input  clock,
  input  left_up,
  input  [15:0] adress_bus,
  input  right_up,
  input  right_down,
  input  left_down,
  input  finnish_turn,
  output is_active,
  output [15:0] data,
  output [5:0] raw_state,
  output [5:0] register_state
);

  wire button_1_out, not_1_out, pull_resistor_1_node, register_1_q, register_2_q, reset_state;
  wire [15:15] pull_resistor_2_node;

  Register #(.width(1)) register_1 (
    .D(is_active), .en(1'b1), .Q(register_1_q), .clk(clock), .clr(pull_resistor_1_node));
  Register #(.width(1), .trigger("low")) register_2 (
    .D(register_1_q), .en(1'b1), .Q(register_2_q), .clk(clock), .clr(pull_resistor_1_node));
  Pull_Resistor pull_resistor_1 (.node(pull_resistor_1_node));
  and and_1 (reset_state, 1'b1, register_2_q);
  D_Flip_Flop d_ff_1 (.clk(left_up), .D(1'b1), .Q(raw_state[2]), .reset(reset_state));  // open: Qn, preset, en
  D_Flip_Flop d_ff_2 (.clk(left_down), .D(1'b1), .Q(raw_state[4]), .reset(reset_state));  // open: Qn, preset, en
  Clock clock_1 ();  // open: out
  D_Flip_Flop d_ff_3 (.clk(checker_select), .D(1'b1), .Q(raw_state[0]), .reset(reset_state));  // open: Qn, preset, en
  D_Flip_Flop d_ff_4 (.clk(finnish_turn), .D(1'b1), .Q(raw_state[5]), .reset(reset_state));  // open: Qn, preset, en
  D_Flip_Flop d_ff_5 (.clk(right_up), .D(1'b1), .Q(raw_state[1]), .reset(reset_state));  // open: Qn, preset, en
  D_Flip_Flop d_ff_6 (.clk(right_down), .D(1'b1), .Q(raw_state[3]), .reset(reset_state));  // open: Qn, preset, en
  // Probe on register_state
  Register #(.width(6)) register_3 (.D(raw_state), .en(1'b1), .Q(register_state), .clk(clock), .clr(reset_state));
  Pull_Resistor pull_resistor_2 (.node(pull_resistor_2_node[15]));
  not not_1 (not_1_out, adress_bus[0]);
  and and_2 (is_active, not_1_out, adress_bus[1], adress_bus[2], adress_bus[3], adress_bus[4], adress_bus[5], adress_bus[6], adress_bus[7], adress_bus[9], adress_bus[10], adress_bus[11], adress_bus[12], adress_bus[13], adress_bus[14], adress_bus[15], adress_bus[8]);
  Button button_1 (.out(button_1_out));
  assign data = is_active ? {{10{pull_resistor_2_node[15]}}, register_state} : 16'bz;  // Controlled_Buffer controlled_buffer_1

  // Other names for the same wires on the sheet: data_bus[15:0] = data; finish_turn = finnish_turn

  // Notes on the sheet:
  //   inputs
  //   outputs
  //   buttons
endmodule
